// Logisim project Timer_project.circ as structural Verilog
module main (
  input  S_S,
  input  M,
  input  S,
  input  PAUSE,
  input  CLK,
  output [3:0] ANODES,
  output [6:0] CATHODES,
  output ALARM
);

  wire cascaded_counters_1_carry, command_unit_1_hold, command_unit_1_increment_min,
       command_unit_1_increment_sec, command_unit_1_reset, command_unit_1_up_or_down,
       debouncer_1_button_debounced, debouncer_2_button_debounced, debouncer_3_button_debounced,
       debouncer_4_button_debounced, freq_divider_1_divided_clock, or_gate_1_c;
  wire [15:0] cascaded_counters_1_q_cascaded;

  Debouncer debouncer_1 (.button(S_S), .clk(CLK), .button_debounced(debouncer_1_button_debounced));
  Debouncer debouncer_2 (.button(M), .clk(CLK), .button_debounced(debouncer_2_button_debounced));
  Debouncer debouncer_3 (.button(S), .clk(CLK), .button_debounced(debouncer_3_button_debounced));
  Debouncer debouncer_4 (.button(PAUSE), .clk(CLK), .button_debounced(debouncer_4_button_debounced));
  Freq_Divider freq_divider_1 (.clock(CLK), .divided_clock(freq_divider_1_divided_clock));
  Command_Unit command_unit_1 (
    .START_STOP(debouncer_1_button_debounced), .M(debouncer_2_button_debounced),
    .S(debouncer_3_button_debounced), .PAUSE(debouncer_4_button_debounced),
    .CARRY(cascaded_counters_1_carry), .CLOCK(CLK), .RESET(command_unit_1_reset), .HOLD(command_unit_1_hold),
    .INCREMENT_MIN(command_unit_1_increment_min), .UP_OR_DOWN(command_unit_1_up_or_down),
    .INCREMENT_SEC(command_unit_1_increment_sec), .ALARM(ALARM));
  OR_GATE or_gate_1 (.A(command_unit_1_increment_sec), .B(freq_divider_1_divided_clock), .C(or_gate_1_c));
  Cascaded_Counters cascaded_counters_1 (
    .reset(command_unit_1_reset), .enable_cascaded(command_unit_1_hold),
    .incmin(command_unit_1_increment_min), .up_or_down(command_unit_1_up_or_down),
    .clock_cascaded(or_gate_1_c), .carry(cascaded_counters_1_carry),
    .Q_cascaded(cascaded_counters_1_q_cascaded));
  Display_7segment display_7segment_1 (
    .S0(cascaded_counters_1_q_cascaded[3:0]), .S1(cascaded_counters_1_q_cascaded[7:4]),
    .M0(cascaded_counters_1_q_cascaded[11:8]), .M1(cascaded_counters_1_q_cascaded[15:12]), .clock(CLK),
    .anode(ANODES), .cathode(CATHODES));
endmodule

// VHDL entity Counter_S0, as the project stores it:
LIBRARY ieee;
USE ieee.std_logic_1164.all;
USE ieee.std_logic_unsigned.all
;

ENTITY Counter_S0 IS
  PORT (
  		clock_S0, enable_S0, incmin, up_or_down, reset: IN std_logic;
  		Q_S0: OUT std_logic_vector(3 downto 0); --reversible counter modulo 10 (0-9, on 4 bits) 
  		carry: OUT std_logic
    );
END Counter_S0;

ARCHITECTURE TypeArchitecture OF Counter_S0 IS

BEGIN

	process(clock_S0)
	
	variable internal_state: std_logic_vector(3 downto 0) := "0000";
	variable internal_carry: std_logic := '0';
	
	begin
	
	if(enable_S0 = '1') then
		if(reset = '1') then internal_state := "0000"; --reset with 0
		elsif(rising_edge(clock_S0)) then
			if(up_or_down = '1') then --count up
				if(internal_state = "1001") then internal_state := "0000";
				else internal_state := internal_state + 1;
				end if;
				if(internal_state = "0000") then internal_carry := '1'; --finish counting in the loop 0-9
				else internal_carry := '0';
				end if;
			else --count down
				if(internal_state = "0000") then internal_state := "1001";
				else internal_state := internal_state - 1;
				end if;
				if(internal_state = "1001") then internal_carry := '1'; --finish counting in the loop 9-0
				else internal_carry := '0';
				end if;
			end if;

		end if;

	end if;

	Q_S0 <= internal_state;
	carry <= internal_carry;

	end process;
	
END TypeArchitecture;

// VHDL entity Counter_S1, as the project stores it:
LIBRARY ieee;
USE ieee.std_logic_1164.all;
USE ieee.std_logic_unsigned.all;

ENTITY Counter_S1 IS
  PORT (
  		clock_S1, enable_S1, incmin, up_or_down, reset: IN std_logic;
  		Q_S1: OUT std_logic_vector(3 downto 0); --reversible counter modulo 6 (0-5, on 4 bits)
  		carry: OUT std_logic
    );
END Counter_S1;

ARCHITECTURE TypeArchitecture OF Counter_S1 IS

BEGIN

	process(clock_S1)
	
	variable internal_state: std_logic_vector(3 downto 0) := "0000";
	variable internal_carry: std_logic := '0';
	
	begin
	
	if(enable_S1 = '1') then
		if(reset = '1') then internal_state := "0000"; --reset with 0
		elsif(rising_edge(clock_S1)) then
			if(up_or_down = '1') then --count up
				if(internal_state = "0101") then internal_state := "0000";
				else internal_state := internal_state + 1;
				end if;
				if(internal_state = "0000") then internal_carry := '1'; --finish counting in the loop 0-5
				else internal_carry := '0';
				end if;
			else --count down
				if(internal_state = "0000") then internal_state := "0101";
				else internal_state := internal_state - 1;
				end if;
				if(internal_state = "0101") then internal_carry := '1'; --finish counting in the loop 5-0
				else internal_carry := '0';
				end if;
			end if;

		end if;

	end if;

	Q_S1 <= internal_state;
	carry <= internal_carry;

	end process;
	
END TypeArchitecture;

// VHDL entity Counter_M0, as the project stores it:
LIBRARY ieee;
USE ieee.std_logic_1164.all;
USE ieee.std_logic_unsigned.all;

ENTITY Counter_M0 IS
  PORT (
  		clock_M0, enable_M0, incmin, up_or_down, reset: IN std_logic;
  		Q_M0: OUT std_logic_vector(3 downto 0); --reversible counter modulo 10 (0-9, on 4 bits) 
  		carry: OUT std_logic
    );
END Counter_M0;

ARCHITECTURE TypeArchitecture OF Counter_M0 IS

BEGIN

	process(clock_M0)
	
	variable internal_state: std_logic_vector(3 downto 0) := "0000";
	variable internal_carry: std_logic := '0';
	
	begin
	
	if(enable_M0 = '1') then
		if(reset = '1') then internal_state := "0000"; --reset with 0
		elsif(rising_edge(clock_M0)) then
			if(up_or_down = '1') then --count up
				if(incmin = '1') then internal_state := internal_state + 1;
				end if;
				if(internal_state = "1001") then internal_state := "0000";
				else internal_state := internal_state + 1;
				end if;
				if(internal_state = "0000") then internal_carry := '1'; --finish counting in the loop 0-9
				else internal_carry := '0';
				end if;
			else --count down
				if(internal_state = "0000") then internal_state := "1001";
				else internal_state := internal_state - 1;
				end if;
				if(internal_state = "1001") then internal_carry := '1'; --finish counting in the loop 9-0
				else internal_carry := '0';
				end if;
			end if;

		end if;

	end if;

	Q_M0 <= internal_state;
	carry <= internal_carry;

	end process;
	
END TypeArchitecture;

// VHDL entity Counter_M1, as the project stores it:
LIBRARY ieee;
USE ieee.std_logic_1164.all;
USE ieee.std_logic_unsigned.all;

ENTITY Counter_M1 IS
  PORT (
  		clock_M1, enable_M1, incmin, up_or_down, reset: IN std_logic;
  		Q_M1: OUT std_logic_vector(3 downto 0); --reversible counter modulo 10 (0-9, on 4 bits) 
  		carry: OUT std_logic
    );
END Counter_M1;

ARCHITECTURE TypeArchitecture OF Counter_M1 IS

BEGIN

	process(clock_M1)
	
	variable internal_state: std_logic_vector(3 downto 0) := "0000";
	variable internal_carry: std_logic := '0';
	
	begin
	
	if(enable_M1 = '1') then
		if(reset = '1') then internal_state := "0000"; --reset with 0
		elsif(rising_edge(clock_M1)) then
			if(up_or_down = '1') then --count up
				if(internal_state = "1001") then internal_state := "0000";
				else internal_state := internal_state + 1;
				end if;
				if(internal_state = "0000") then internal_carry := '1'; --finish counting in the loop 0-9
				else internal_carry := '0';
				end if;
			else --count down
				if(internal_state = "0000") then internal_state := "1001";
				else internal_state := internal_state - 1;
				end if;
				if(internal_state = "1001") then internal_carry := '1'; --finish counting in the loop 9-0
				else internal_carry := '0';
				end if;
			end if;
			
		end if;

	end if;

	Q_M1 <= internal_state;
	carry <= internal_carry;

	end process;
	
END TypeArchitecture;

// VHDL entity Cascaded_Counters, as the project stores it:
LIBRARY ieee;
USE ieee.std_logic_1164.all;

ENTITY Cascaded_Counters IS
  PORT (
 	reset, 
enable_cascaded, incmin, up_or_down: IN std_logic;
  	clock_cascaded: IN std_logic;
  	carry: OUT std_logic;
  	Q_cascaded: OUT std_logic_vector(15 downto 0)  --the output will be all the counters concatenated, all the numbers are "linked"
    );
END Cascaded_Counters;

ARCHITECTURE TypeArchitecture OF Cascaded_Counters IS

COMPONENT Counter_S0 is 
PORT (
  		clock_S0, enable_S0, incmin, up_or_down, reset: IN std_logic;
  		Q_S0: OUT std_logic_vector(3 downto 0); --reversible counter modulo 10 (0-9, on 4 bits) 
  		carry: OUT std_logic
    );
END COMPONENT;

COMPONENT Counter_S1 is
PORT (
  		clock_S1, enable_S1, incmin, up_or_down, reset: IN std_logic;
  		Q_S1: OUT std_logic_vector(3 downto 0); --reversible counter modulo 6 (0-5, on 4 bits)
  		carry: OUT std_logic
    );
END COMPONENT;

COMPONENT Counter_M0 is
PORT (
  		clock_M0, enable_M0, incmin, up_or_down, reset: IN std_logic;
  		Q_M0: OUT std_logic_vector(3 downto 0); --reversible counter modulo 10 (0-9, on 4 bits) 
  		carry: OUT std_logic
    );
END COMPONENT;

COMPONENT Counter_M1 is
PORT (
  		clock_M1, enable_M1, incmin, up_or_down, reset: IN std_logic;
  		Q_M1: OUT std_logic_vector(3 downto 0); --reversible counter modulo 10 (0-9, on 4 bits) 
  		carry: OUT std_logic
    );
END COMPONENT;

signal internal_state: std_logic_vector(15 downto 0); 
signal carry_S0, carry_S1, carry_M0, carry_M1: std_logic;

BEGIN

C_S0: Counter_S0 port map(
		clock_S0 => clock_cascaded, enable_S0 => enable_cascaded, incmin => incmin, up_or_down => up_or_down, reset => reset,
		Q_S0 =>  internal_state(3 downto 0), carry => carry_S0);

C_S1: Counter_S1 port map(
		clock_S1 => carry_S0, enable_S1 => enable_cascaded, incmin => incmin, up_or_down => up_or_down, reset => reset,
		Q_S1 => internal_state(7 downto 4), carry => carry_S1 );

C_M0: Counter_M0 port map(
		clock_M0 => carry_S1, enable_M0 => enable_cascaded, incmin => incmin, up_or_down => up_or_down, reset => reset,
		Q_M0 => internal_state(11 downto 8), carry => carry_M0 );

C_M1: Counter_M1 port map(
		clock_M1=> carry_M0, enable_M1=> enable_cascaded, incmin => incmin, up_or_down => up_or_down, reset => reset,
		Q_M1 => internal_state(15 downto 12), carry => carry_M1 );

Q_cascaded <= internal_state;
carry <= carry_M1;

END TypeArchitecture;


LIBRARY ieee;
USE ieee.std_logic_1164.all;
USE ieee.std_logic_unsigned.all
;

ENTITY Counter_S0 IS
  PORT (
  		clock_S0, enable_S0, incmin, up_or_down, reset: IN std_logic;
  		Q_S0: OUT std_logic_vector(3 downto 0); --reversible counter modulo 10 (0-9, on 4 bits) 
  		carry: OUT std_logic
    );
END Counter_S0;

ARCHITECTURE TypeArchitecture OF Counter_S0 IS

BEGIN

	process(clock_S0)
	
	variable internal_state: std_logic_vector(3 downto 0) := "0000";
	variable internal_carry: std_logic := '0';
	
	begin
	
	if(enable_S0 = '1') then
		if(reset = '1') then internal_state := "0000"; --reset with 0
		elsif(rising_edge(clock_S0)) then
			if(up_or_down = '1') then --count up
				if(internal_state = "1001") then internal_state := "0000";
				else internal_state := internal_state + 1;
				end if;
				if(internal_state = "0000") then internal_carry := '1'; --finish counting in the loop 0-9
				else internal_carry := '0';
				end if;
			else --count down
				if(internal_state = "0000") then internal_state := "1001";
				else internal_state := internal_state - 1;
				end if;
				if(internal_state = "1001") then internal_carry := '1'; --finish counting in the loop 9-0
				else internal_carry := '0';
				end if;
			end if;

		end if;

	end if;

	Q_S0 <= internal_state;
	carry <= internal_carry;

	end process;
	
END TypeArchitecture;


LIBRARY ieee;
USE ieee.std_logic_1164.all;
USE ieee.std_logic_unsigned.all;

ENTITY Counter_S1 IS
  PORT (
  		clock_S1, enable_S1, incmin, up_or_down, reset: IN std_logic;
  		Q_S1: OUT std_logic_vector(3 downto 0); --reversible counter modulo 6 (0-5, on 4 bits)
  		carry: OUT std_logic
    );
END Counter_S1;

ARCHITECTURE TypeArchitecture OF Counter_S1 IS

BEGIN

	process(clock_S1)
	
	variable internal_state: std_logic_vector(3 downto 0) := "0000";
	variable internal_carry: std_logic := '0';
	
	begin
	
	if(enable_S1 = '1') then
		if(reset = '1') then internal_state := "0000"; --reset with 0
		elsif(rising_edge(clock_S1)) then
			if(up_or_down = '1') then --count up
				if(internal_state = "0101") then internal_state := "0000";
				else internal_state := internal_state + 1;
				end if;
				if(internal_state = "0000") then internal_carry := '1'; --finish counting in the loop 0-5
				else internal_carry := '0';
				end if;
			else --count down
				if(internal_state = "0000") then internal_state := "0101";
				else internal_state := internal_state - 1;
				end if;
				if(internal_state = "0101") then internal_carry := '1'; --finish counting in the loop 5-0
				else internal_carry := '0';
				end if;
			end if;

		end if;

	end if;

	Q_S1 <= internal_state;
	carry <= internal_carry;

	end process;
	
END TypeArchitecture;


LIBRARY ieee;
USE ieee.std_logic_1164.all;
USE ieee.std_logic_unsigned.all;

ENTITY Counter_M0 IS
  PORT (
  		clock_M0, enable_M0, incmin, up_or_down, reset: IN std_logic;
  		Q_M0: OUT std_logic_vector(3 downto 0); --reversible counter modulo 10 (0-9, on 4 bits) 
  		carry: OUT std_logic
    );
END Counter_M0;

ARCHITECTURE TypeArchitecture OF Counter_M0 IS

BEGIN

	process(clock_M0)
	
	variable internal_state: std_logic_vector(3 downto 0) := "0000";
	variable internal_carry: std_logic := '0';
	
	begin
	
	if(enable_M0 = '1') then
		if(reset = '1') then internal_state := "0000"; --reset with 0
		elsif(rising_edge(clock_M0)) then
			if(up_or_down = '1') then --count up
				if(incmin = '1') then internal_state := internal_state + 1;
				end if;
				if(internal_state = "1001") then internal_state := "0000";
				else internal_state := internal_state + 1;
				end if;
				if(internal_state = "0000") then internal_carry := '1'; --finish counting in the loop 0-9
				else internal_carry := '0';
				end if;
			else --count down
				if(internal_state = "0000") then internal_state := "1001";
				else internal_state := internal_state - 1;
				end if;
				if(internal_state = "1001") then internal_carry := '1'; --finish counting in the loop 9-0
				else internal_carry := '0';
				end if;
			end if;

		end if;

	end if;

	Q_M0 <= internal_state;
	carry <= internal_carry;

	end process;
	
END TypeArchitecture;


LIBRARY ieee;
USE ieee.std_logic_1164.all;
USE ieee.std_logic_unsigned.all;

ENTITY Counter_M1 IS
  PORT (
  		clock_M1, enable_M1, incmin, up_or_down, reset: IN std_logic;
  		Q_M1: OUT std_logic_vector(3 downto 0); --reversible counter modulo 10 (0-9, on 4 bits) 
  		carry: OUT std_logic
    );
END Counter_M1;

ARCHITECTURE TypeArchitecture OF Counter_M1 IS

BEGIN

	process(clock_M1)
	
	variable internal_state: std_logic_vector(3 downto 0) := "0000";
	variable internal_carry: std_logic := '0';
	
	begin
	
	if(enable_M1 = '1') then
		if(reset = '1') then internal_state := "0000"; --reset with 0
		elsif(rising_edge(clock_M1)) then
			if(up_or_down = '1') then --count up
				if(internal_state = "1001") then internal_state := "0000";
				else internal_state := internal_state + 1;
				end if;
				if(internal_state = "0000") then internal_carry := '1'; --finish counting in the loop 0-9
				else internal_carry := '0';
				end if;
			else --count down
				if(internal_state = "0000") then internal_state := "1001";
				else internal_state := internal_state - 1;
				end if;
				if(internal_state = "1001") then internal_carry := '1'; --finish counting in the loop 9-0
				else internal_carry := '0';
				end if;
			end if;
			
		end if;

	end if;

	Q_M1 <= internal_state;
	carry <= internal_carry;

	end process;
	
END TypeArchitecture;

// VHDL entity Freq_Divider, as the project stores it:
LIBRARY ieee;
USE ieee.std_logic_1164.all;

ENTITY Freq_Divider IS
 --divides from 100 MHz to 1 Hz; 100 MHz = 100.000.000 Hz
  PORT (
  
	clock: IN std_logic;
  	divided_clock: OUT std_logic
    );
END Freq_Divider;

ARCHITECTURE TypeArchitecture OF Freq_Divider IS

signal count: INTEGER := 1;
signal clk: std_logic;

BEGIN

process(clock)
begin
	if(rising_edge(clock)) then
		if(count < 49999999) then count <= count + 1;
		elsif(count = 49999999) then count <= 0;
		clk <= not clk;
		end if;
	end if;
end process;

divided_clock <= clk;

END TypeArchitecture;

// VHDL entity Display_7segment, as the project stores it:
LIBRARY IEEE;
USE ieee.std_logic_1164.all;
USE ieee.std_logic_unsigned.all;

ENTITY Display_7segment IS
  PORT (
  	S0, S1, M0, M1: IN std_logic_vector(3 downto 0);
  	anode: OUT std_logic_vector(3 downto 0);
  	clock: IN std_logic;
  	cathode: OUT std_logic_vector(6 downto 0)
    );
END Display_7segment;

ARCHITECTURE TypeArchitecture OF Display_7segment IS

signal count: std_logic_vector(15 downto 0);
signal number: std_logic_vector(3 downto 0);

BEGIN


process(clock)
begin
	if (rising_edge(clock)) then count <= count + 1;
	end if;
end process;

--choosing the anode

process(count)
begin
	case(count(15 downto 14)) is
		when "00" => anode <= not "1110";
		when "01" => anode <= not "1101";
		when "10" => anode <= not "1011";
		when others => anode <= not "0111";
	end case;
end process;

--choosing the digits

process(count, S0, S1, M0, M1)
begin
	case(count(15 downto 14)) is
		when "00" => number <= S0;
		when "01" => number <= S1;
		when "10" => number <= M0;
		when others => number <= M1;
	end case;
end process;

--7 Segment BCD Decoder

process(number)
begin
	case number is
	when "0000" => cathode <= not "0000001"; --0
	when "0001" => cathode <= not "1001111"; --1
	when "0010" => cathode <= not "0010010"; --2
	when "0011" => cathode <= not "0000110"; --3
	when "0100" => cathode <= not "1001100"; --4
	when "0101" => cathode <= not "0100100"; --5
	when "0110" => cathode <= not "0100000"; --6
	when "0111" => cathode <= not "0001111"; --7
	when "1000" => cathode <= not "0000000"; --8
	when "1001" => cathode <= not "0000100"; --9
	when others => cathode <= not "0000001"; --0
	end case;
end process;
	
END TypeArchitecture;

// VHDL entity Debouncer, as the project stores it:
LIBRARY IEEE;
USE IEEE.STD_LOGIC_1164.ALL;
 
ENTITY Debouncer IS
PORT (
	button: IN std_logic;
	clk: IN std_logic;
	button_debounced: OUT std_logic);
END Debouncer;
 
ARCHITECTURE TypeArchitecture OF Debouncer IS

COMPONENT D_ff IS
PORT (
  D, clock: in std_logic;
  Q: out std_logic
    );
END COMPONENT;

signal Q0: std_logic := '0';
signal Q1: std_logic := '0';
signal Q2: std_logic := '0'; 

BEGIN

LINK1: D_ff port map(D => button, clock => clk, Q => Q0);
LINK2: D_ff port map(D => Q0, clock => clk, Q => Q1);
LINK3: D_ff port map(D => Q1, clock => clk, Q => Q2);

button_debounced <= Q0 and Q1 and Q2;

 
END TypeArchitecture;


LIBRARY ieee;
USE ieee.std_logic_1164.all;

ENTITY D_ff IS
PORT (
  D, clock: in std_logic;
  Q: out std_logic
    );
END D_ff;


ARCHITECTURE TypeArchitecture OF D_ff IS

BEGIN

process(clock)

begin
	if(rising_edge(clock)) then Q <= D;
	end if;
end process;

END TypeArchitecture;

// VHDL entity Command_Unit, as the project stores it:
LIBRARY ieee;
USE ieee.std_logic_1164.all;

ENTITY Command_Unit IS
  PORT ( 	
	START_STOP, M, S, PAUSE, CARRY: IN std_logic; -- user inputs = "buttons"; CARRY = resources input, activated when we reach 0 by counting down
  	CLOCK: in std_logic;
  	RESET, HOLD, INCREMENT_MIN, UP_OR_DOWN, INCREMENT_SEC, ALARM: OUT std_logic -- outputs 
    );
END Command_Unit;

ARCHITECTURE TypeArchitecture OF Command_Unit IS

type STATE_T is (S_RESET,S_0, S_COUNT_UP, S_HOLD_UP, S_INCREMENT_MIN, S_INCREMENT_SEC, S_SHOW, S_UP_OR_DOWN,  S_COUNT_DOWN, S_ALARM);
signal STATE, NEXT_STATE:  STATE_T := S_0;

BEGIN

UPDATE_STATE: process (S, M, CLOCK)
		    begin 

		    		if(S = '1' and M = '1') then
		    		    STATE <= S_0;
		    		elsif(rising_edge(CLOCK)) then 
		    		    STATE <= NEXT_STATE;
		    		end if;
		    	end process UPDATE_STATE;

TRANSITIONS: process (STATE, START_STOP, M, S, PAUSE, CARRY)
		   begin

		   		case STATE is
		   			when S_0 => HOLD <= '1';
		   					  INCREMENT_MIN <= '0'; 
		   					  INCREMENT_SEC <= '0';
		   				       UP_OR_DOWN <= '1'; 
		   				       ALARM <= '0';
		   				       RESET <= '1';
		   				if(START_STOP = '0') then NEXT_STATE <= S_0;
		   				else NEXT_STATE <= S_COUNT_UP;
		   				end if;

		   			when S_COUNT_UP => UP_OR_DOWN <= '1';
		   			                   HOLD <= '1'; -- enable becomes 1, so the counters are working
		   			                   INCREMENT_MIN <= '0'; 
		   			                   INCREMENT_SEC <= '0';
		   						    ALARM <= '0';
		   						    RESET <= '0';
		   				if(PAUSE = '1') then NEXT_STATE <= S_HOLD_UP;
		   				elsif (M = '1') then NEXT_STATE <= S_INCREMENT_MIN;
		   				elsif (S = '1') then NEXT_STATE <= S_INCREMENT_SEC;
		   				else NEXT_STATE <= S_COUNT_UP;
		   				end if;

		   			when S_HOLD_UP => HOLD <= '0';  -- enable becomes 0, so the counters stop
		   						   INCREMENT_MIN <= '0'; 
		   						   INCREMENT_SEC <= '0';
		   						   UP_OR_DOWN <= '1'; 
		   						   ALARM <= '0';
		   						   RESET <= '0';
		   				if(START_STOP = '1') then NEXT_STATE <= S_COUNT_UP;
		   				else NEXT_STATE <= S_HOLD_UP;
		   				end if;

		   			when S_INCREMENT_MIN => INCREMENT_MIN <= '1';
		   			                        HOLD <= '1'; 
		   			                        INCREMENT_SEC <= '0';
		   							    UP_OR_DOWN <= '1'; 
		   							    ALARM <= '0';
		   							    RESET <= '0';
		   							    NEXT_STATE <= S_SHOW;
						
		   			when S_INCREMENT_SEC => INCREMENT_SEC <= '1'; 
		   			                        HOLD <= '1'; 
		   			                        INCREMENT_MIN <= '0';
		   							    UP_OR_DOWN <= '1'; 
		   							    ALARM <= '0';
		   							    RESET <= '0';
		   				      		    NEXT_STATE <= S_SHOW;

		   			when S_SHOW => HOLD <= '0'; 
								INCREMENT_MIN <= '0'; 
								INCREMENT_SEC <= '0';
		   						UP_OR_DOWN <= '1';  
		   						ALARM <= '0';
		   						RESET <= '0';
		   				if(START_STOP = '0') then NEXT_STATE <= S_SHOW;
		   		     	else NEXT_STATE <= S_COUNT_DOWN;
						end if;
								
								
		   			when S_COUNT_DOWN => UP_OR_DOWN <='0';
		   			                     HOLD <= '1'; 
		   			                     INCREMENT_MIN <= '0'; 
		   			                     INCREMENT_SEC <= '0';
		   		                          ALARM <= '0';
		   		                          RESET <= '0';
		   		          if(CARRY = '0') then NEXT_STATE <= S_COUNT_DOWN;
		   				else  NEXT_STATE <= S_ALARM;
		   				end if;
		   							
		   			when S_ALARM => ALARM <= '1';
		   			                HOLD <= '1'; 
		   			                INCREMENT_MIN <= '0'; 
		   			                INCREMENT_SEC <= '0';
		   		                     UP_OR_DOWN <= '0'; 
		   		                     RESET <= '1';
		   		          if(START_STOP = '0') then NEXT_STATE <= S_ALARM;
		   				else NEXT_STATE <= S_0;
		   				end if;
		   				
		   			when others => null;
		   				
		   		end case;
		   		
		  end process TRANSITIONS;		
		   				
END TypeArchitecture;

// VHDL entity OR_GATE, as the project stores it:
LIBRARY ieee;
USE ieee.std_logic_1164.all;

ENTITY OR_GATE IS
  PORT (
  	A,B: IN STD_LOGIC;
  	C: OUT STD_LOGIC
    );
END OR_GATE;


ARCHITECTURE TypeArchitecture OF OR_GATE IS

BEGIN

C <= A or B;

END TypeArchitecture;

// VHDL entity D_ff, as the project stores it:
LIBRARY ieee;
USE ieee.std_logic_1164.all;

ENTITY D_ff IS
PORT (
  D, clock: in std_logic;
  Q: out std_logic
    );
END D_ff;


ARCHITECTURE TypeArchitecture OF D_ff IS

BEGIN

process(clock)

begin
	if(rising_edge(clock)) then Q <= D;
	end if;
end process;

END TypeArchitecture;
